# Fritzing sketch control-things-from-the-internet (saved by Fritzing 0.9.2b)
breadboards: 1

parts:
  Part1 = Arduino Uno (Rev3)
  T1 = LM35 Temperature Sensor [package="TO92 [THT]"]
  LED1 = LED - 5mm [color="Red (633nm)" package="5 mm [THT]"]
  J1 = Basic Servo
  R1 = Photocell (LDR) [package=THT]
  R2 = Resistor [tolerance=±5% resistance=220 package=THT]

nets:
  N1: Part1.A0, T1.+Vs
  N2: Part1.A2, R1.pin_0, R2.Pin_1
  N3: Part1.D13/SCK, LED1.anode
  GND: Part1.GND, T1.GND, LED1.cathode, J1.gnd, R1.pin_1
  N4: Part1.D6_PWM, J1.pulse
  5V: Part1.5V, T1.Vout, J1.vcc, R2.Pin_0
